// Logisim project proc_RAM.circ as structural Verilog: 1 circuit, main circuit main
module main (
);

  wire Cl, data_ins_prime, memory, not_1_out, read_write_prime;
  wire [7:0] addr, cdm_8_mark5_1_p6, cdm_8_mark5_1_p7, D;

  // Debugger debugger_1: pin names not known
  Clock clock_1 (.out(Cl));
  // CdM_8_mark5 cdm_8_mark5_1: pin names not known; wires that end beside it: Cl, data_ins_prime, memory, read_write_prime, addr, cdm_8_mark5_1_p6, cdm_8_mark5_1_p7
  assign D = not_1_out ? cdm_8_mark5_1_p6 : 8'bz;  // Controlled_Buffer controlled_buffer_1
  not not_1 (not_1_out, read_write_prime);
  assign cdm_8_mark5_1_p7 = read_write_prime ? D : 8'bz;  // Controlled_Buffer controlled_buffer_2
  RAM ram_1 (.addr(addr), .data(D), .sel(memory), .clk(Cl), .ld(read_write_prime));  // open: clr
endmodule
